# Fritzing sketch pir (saved by Fritzing 0.9.3b)
breadboards: 1

parts:
  part = Arduino Uno (Rev3)
  LED1 = LED - 5mm [color="Red (633nm)" package="5 mm [THT]"]
  LED2 = LED - 5mm [color="Red (633nm)" package="5 mm [THT]"]
  PIR = Infrared Proximity Sensor
  R1 = Resistor [tolerance=±5% resistance=220 package=THT]
  R2 = Resistor [tolerance=±5% resistance=220 package=THT]
  R3 = Resistor [tolerance=±5% resistance=10k package=THT]
  Potentiomètre = Trimmer Potentiometer [maximum_resistance=10kΩ package=THT]

nets:
  N1: part.A0, Potentiomètre.leg1
  N2: part.D8, LED2.anode
  N3: part.D9_PWM, LED1.anode
  GND: part.GND, PIR.GND, Potentiomètre.wiper
  N4: part.D7, PIR.Vout, R3.Pin_0
  5V: part.5V, PIR.Vcc, R3.Pin_1, Potentiomètre.leg2
  N5: LED1.cathode, R1.Pin_1
  N6: LED2.cathode, R2.Pin_1
